// Logisim project angulaire.circ as structural Verilog: 3 circuits, main circuit main
module main (
  input  CHA,
  input  CHB,
  input  CHC,
  output dir,
  output en_cnt,
  output Selected
);

  wire clock_1_out, d_ff_1_q, d_ff_2_q, debounce_1_filtered, debounce_2_filtered;

  Clock clock_1 (.out(clock_1_out));
  debounce debounce_1 (.raw(CHA), .clck(clock_1_out), .filtered(debounce_1_filtered));
  debounce debounce_2 (.raw(CHB), .clck(clock_1_out), .filtered(debounce_2_filtered));
  debounce debounce_3 (.raw(CHC), .clck(clock_1_out), .filtered(Selected));
  D_Flip_Flop d_ff_1 (.D(debounce_1_filtered), .clk(clock_1_out), .Q(d_ff_1_q));  // open: Qn, preset, reset
  D_Flip_Flop d_ff_2 (.D(debounce_2_filtered), .clk(clock_1_out), .Q(d_ff_2_q));  // open: Qn, preset, reset
  decodeur decodeur_1 (
    .Bp(d_ff_2_q), .Ap(d_ff_1_q), .Bc(debounce_2_filtered), .Ac(debounce_1_filtered), .dir(dir),
    .en_cnt(en_cnt));
endmodule

module debounce (
  input  raw,
  input  clck,
  output filtered
);

  wire and_1_out, and_2_out, d_ff_1_q, d_ff_2_q, d_ff_3_q, d_ff_4_q;

  D_Flip_Flop d_ff_1 (.D(raw), .clk(clck), .Q(d_ff_1_q));  // open: Qn, preset, reset
  D_Flip_Flop d_ff_2 (.D(d_ff_1_q), .clk(clck), .Q(d_ff_2_q));  // open: Qn, preset, reset
  D_Flip_Flop d_ff_3 (.D(d_ff_2_q), .clk(clck), .Q(d_ff_3_q));  // open: Qn, preset, reset
  D_Flip_Flop d_ff_4 (.D(d_ff_3_q), .clk(clck), .Q(d_ff_4_q));  // open: Qn, preset, reset
  and and_1 (and_1_out, d_ff_2_q, d_ff_3_q, d_ff_4_q);
  and and_2 (and_2_out, ~d_ff_4_q, ~d_ff_3_q, ~d_ff_2_q);  // AND_Gate
  J_K_Flip_Flop j_k_ff_1 (.J(and_1_out), .K(and_2_out), .clk(clck), .Q(filtered));  // open: Qn, preset, reset
endmodule

module decodeur (
  input  Bp,
  input  Ap,
  input  Bc,
  input  Ac,
  output dir,
  output en_cnt
);

  wire and_1_out, and_2_out, and_3_out, and_4_out, and_5_out, and_6_out, not_1_out, not_2_out, not_3_out,
       not_4_out;

  not not_1 (not_1_out, Bp);
  not not_2 (not_2_out, Ap);
  not not_3 (not_3_out, Bc);
  not not_4 (not_4_out, Ac);
  and and_1 (and_1_out, not_2_out, not_3_out);
  and and_2 (and_2_out, Ap, Bc);
  and and_3 (and_3_out, not_2_out, Ac);
  and and_4 (and_4_out, not_1_out, Bc);
  and and_5 (and_5_out, Ap, not_4_out);
  and and_6 (and_6_out, Bp, not_3_out);
  or or_1 (dir, and_1_out, and_2_out);
  or or_2 (en_cnt, and_3_out, and_4_out, and_5_out, and_6_out);
endmodule
